# Fritzing sketch sample (saved by Fritzing 0.9.3b)
circuit board: 15.24cm x 10.16cm

parts:
  R1 = Resistor [tolerance=±5% resistance=220 package=THT]
  R2 = Resistor [tolerance=±5% resistance=220 package=THT]
  R3 = Resistor [tolerance=±5% resistance=220 package=THT]
  LED1 = RGB LED (com. cathode, rgb) [package="5 mm [THT]"]
  Raspberry_Pi_Zero1 = Raspberry Pi Zero (for pcb)

nets:
  N1: R1.Pin_0, LED1.red_anode
  N2: R1.Pin_1, Raspberry_Pi_Zero1.GIPO17
  N3: R2.Pin_0, LED1.green_anode
  N4: R2.Pin_1, Raspberry_Pi_Zero1.GIPO27
  N5: R3.Pin_0, LED1.blue_anode
  N6: R3.Pin_1, Raspberry_Pi_Zero1.GIPO22
  N7: LED1.common_cathode, Raspberry_Pi_Zero1.GND

custom parts:
  Raspberry Pi Zero (for pcb): The Raspberry Pi Zero is half the size of a Model A+, with twice the utility. A tiny Raspberry Pi that’s affordable enough for any project! · 1Ghz, Single-core CPU · 512MB RAM · Mini HDMI and USB On-The-Go ports · Micro USB power · HAT-compatible 40-pin header
